# Fritzing sketch HeartbeatStationBoard (saved by Fritzing 0.9.4)
circuit board: 5.9cm x 8.6cm
breadboards: 1

parts:
  DFRobot_DFPlayer_Mini1 = DFRobot DFPlayer Mini [part_number=DFR0299]
  SP1 = SPEAKER [package=pcb_mount_speaker]  # not connected
  R1 = Resistor [tolerance=±5% resistance=10 package=THT]
  Speaker = female pin header, 3 pins [form="♀ (female)"]
  LED_0 = molex pin header, 5 pins [form=molex]
  Power = female alternating pin header, 2 pins [form="♀ (female)"]
  Vol = Trimmer Potentiometer [maximum_resistance=100kΩ package=THT]
  Part1 = Arduino Uno (Rev3)

nets:
  VCC: DFRobot_DFPlayer_Mini1.VCC, LED_0.pin4, LED_0.pin5, Vol.leg2, Part1.5V
  N1: DFRobot_DFPlayer_Mini1.RX, R1.Pin_1
  N2: DFRobot_DFPlayer_Mini1.TX, Part1.D10_PWM/SS
  N3: DFRobot_DFPlayer_Mini1.SPK_1, Speaker.pin1
  N4: DFRobot_DFPlayer_Mini1.GND-1, DFRobot_DFPlayer_Mini1.GND-2, Speaker.pin2, LED_0.pin3, Power.pin2, Vol.leg1, Part1.GND
  N5: DFRobot_DFPlayer_Mini1.SPK_2, Speaker.pin3
  N6: R1.Pin_0, Part1.D11_PWM/MOSI
  N7: LED_0.pin1, Part1.D3_PWM
  N8: LED_0.pin2, Part1.D2
  N9: Power.pin1, Part1.VIN
  N10: Vol.wiper, Part1.A2

notes:
  -
  +
