# Fritzing sketch HeartbeatStationBoard_v2 (saved by Fritzing 0.9.4)
circuit board: 5.9cm x 8.6cm
breadboards: 1

parts:
  DFRobot_DFPlayer_Mini1 = DFRobot DFPlayer Mini [part_number=DFR0299]
  SP1 = SPEAKER [package=pcb_mount_speaker]  # not connected
  R1 = Resistor [tolerance=±5% resistance=10 package=THT]
  Speaker = female pin header, 3 pins [form="♀ (female)"]
  LED_0 = molex pin header, 5 pins [form=molex]
  Power = female alternating pin header, 2 pins [form="♀ (female)"]
  Vol = Trimmer Potentiometer [maximum_resistance=100kΩ package=THT]
  J1 = double row female pin header, 16 pins [form="♀ (female)"]
  J2 = double row female pin header, 12 pins [form="♀ (female)"]
  J3 = double row female pin header, 16 pins [form="♀ (female)"]
  J4 = double row female pin header, 20 pins [form="♀ (female)"]

nets:
  N1: DFRobot_DFPlayer_Mini1.VCC, LED_0.pin4, LED_0.pin5, Vol.leg2, J1.pin5, J1.pin12
  N2: DFRobot_DFPlayer_Mini1.RX, R1.Pin_1
  N3: DFRobot_DFPlayer_Mini1.TX, J4.pin8, J4.pin13
  N4: DFRobot_DFPlayer_Mini1.SPK_1, Speaker.pin1
  N5: DFRobot_DFPlayer_Mini1.GND-1, DFRobot_DFPlayer_Mini1.GND-2, Speaker.pin2, LED_0.pin3, Power.pin2, Vol.leg1, J1.pin7, J1.pin10
  N6: DFRobot_DFPlayer_Mini1.SPK_2, Speaker.pin3
  N7: R1.Pin_0, J4.pin7, J4.pin14
  N8: LED_0.pin1, J3.pin5, J3.pin12
  N9: LED_0.pin2, J3.pin6, J3.pin11
  N10: Power.pin1, J1.pin8, J1.pin9
  N11: Vol.wiper, J2.pin3, J2.pin10

notes:
  -
  +
